# Fritzing sketch dth22 (saved by Fritzing 0.9.3b)
breadboards: 1

parts:
  Raspberry_Pi_3 = Raspberry Pi 3 [part_number=RPI-3-V1.2]
  R3 = Resistor [tolerance=±5% resistance=5.1k package=THT]
  DHT1 = DHT22 Humidity and Temperature Sensor
  Q1 = NPN-Transistor [package="SOT-23 [SMD]"]

nets:
  3V3: Raspberry_Pi_3.3v3, R3.Pin_0, DHT1.VDD
  N1: Raspberry_Pi_3.GND, Q1.1
  N2: Raspberry_Pi_3.GIPO17, Q1.0
  N3: Raspberry_Pi_3.GIPO27, R3.Pin_1, DHT1.DATA
  N4: DHT1.GND, Q1.2
