# Fritzing sketch exempleTransistor (saved by Fritzing 0.9.3b)
breadboards: 1

parts:
  Q1 = NPN-Transistor [package="TO92 [THT]"]
  LED1 = LED - 5mm [color="Red (633nm)" package="5 mm [THT]"]
  Raspberry_Pi_3 = Raspberry Pi 3 [part_number=RPI-3-V1.2]
  R1 = Resistor [tolerance=±5% resistance=1k package=THT]

nets:
  N1: Q1.E, Raspberry_Pi_3.3v3
  N2: Q1.B, Raspberry_Pi_3.GIPO17
  N3: Q1.C, LED1.anode
  N4: LED1.cathode, R1.Pin_1
  N5: Raspberry_Pi_3.GND, R1.Pin_0
