# Fritzing sketch feeder (saved by Fritzing 0.9.3b)
breadboards: 1

parts:
  Raspberry_Pi_3 = Raspberry Pi 3 [part_number=RPI-3-V1.2]
  J1 = Basic Servo
  Q2 = NPN-Transistor [package="TO92 [THT]"]
  Q1 = NPN-Transistor [package="TO92 [THT]"]
  R2 = Photocell (LDR) [package=THT]
  R1 = Resistor [tolerance=±5% resistance=5.1k package=THT]

nets:
  N1: Raspberry_Pi_3.3v3, Q2.E, Q1.E
  N2: Raspberry_Pi_3.GIPO17, Q1.B
  N3: Raspberry_Pi_3.GIPO27, R1.Pin_0
  N4: Raspberry_Pi_3.GIPO22, Q2.B
  GND: Raspberry_Pi_3.GND, J1.gnd
  N5: Raspberry_Pi_3.GIPO18, J1.pulse
  N6: J1.vcc, Q2.C
  N7: Q1.C, R2.pin_1
  N8: R2.pin_0, R1.Pin_1
