# Fritzing sketch ldr (saved by Fritzing 0.9.3b)
breadboards: 1

parts:
  Raspberry_Pi_3 = Raspberry Pi 3 [part_number=RPI-3-V1.2]
  R1 = Resistor [tolerance=±5% resistance=5.1k package=THT]
  R2 = Photocell (LDR) [package=THT]
  Q1 = NPN-Transistor [package="TO92 [THT]"]

nets:
  N1: Raspberry_Pi_3.3v3, Q1.E
  N2: Raspberry_Pi_3.GIPO17, Q1.B
  N3: Raspberry_Pi_3.GIPO27, R1.Pin_0
  N4: R1.Pin_1, R2.pin_0
  N5: R2.pin_1, Q1.C
