# Fritzing sketch light (saved by Fritzing 0.9.3b)
breadboards: 1

parts:
  Raspberry_Pi_3 = Raspberry Pi 3 [part_number=RPI-3-V1.2]
  Q1 = NPN-Transistor [package="TO92 [THT]"]
  LED1 = LEDs [package=led10mm]

nets:
  N1: Raspberry_Pi_3.3v3, Q1.C
  N2: Raspberry_Pi_3.GIPO17, Q1.B
  N3: Raspberry_Pi_3.GND, LED1.C
  N4: Q1.E, LED1.A
