# Fritzing sketch project (saved by Fritzing 0.9.3b)
breadboards: 2

parts:
  Raspberry_Pi_3 = Raspberry Pi 3 [part_number=RPI-3-V1.2]
  J1 = Basic Servo
  Q2 = NPN-Transistor [package="TO92 [THT]"]
  Q1 = NPN-Transistor [package="TO92 [THT]"]
  R2 = Photocell (LDR) [package=THT]
  R1 = Resistor [tolerance=±5% resistance=5.1k package=THT]
  VCC1_5v = 4 x AAA Battery Mount
  VCC2 = Battery
  DS1 = DS18B20 1-Wire Temperature Sensor [part_number=DS18B20]
  Q3 = NPN-Transistor [package="TO92 [THT]"]
  R3 = Resistor [tolerance=±5% resistance=5.1k package=THT]
  R4 = Photocell (LDR) [package=THT]
  Q4 = NPN-Transistor [package="TO92 [THT]"]
  R5 = Resistor [tolerance=±5% resistance=5.1k package=THT]
  R6 = Photocell (LDR) [package=THT]
  Q5 = NPN-Transistor [package="SOT-23 [SMD]"]
  DHT2 = DHT22 Humidity and Temperature Sensor
  R7 = Resistor [tolerance=±5% resistance=5.1k package=THT]
  Q6 = NPN-Transistor [package="SOT-23 [SMD]"]
  DHT3 = DHT22 Humidity and Temperature Sensor
  R8 = Resistor [tolerance=±5% resistance=5.1k package=THT]
  Q7 = NPN-Transistor [package="TO92 [THT]"]
  LED4_Light_1 = LEDs [package=led10mm]
  Q8 = NPN-Transistor [package="TO92 [THT]"]
  S2_water_level = Pushbutton [package=THT]
  Q9 = NPN-Transistor [package="TO92 [THT]"]
  Q10 = NPN-Transistor [package="TO92 [THT]"]
  Q11 = NPN-Transistor [package="TO92 [THT]"]
  Q12 = NPN-Transistor [package="TO92 [THT]"]
  Q13 = NPN-Transistor [package="TO92 [THT]"]
  LED1_heater = LED - 5mm [color="Green (570nm)" package="5 mm [THT]"]
  LED2_oxygen_pump = LED - 5mm [color="Yellow (595nm)" package="5 mm [THT]"]
  LED3_second_pump = LED - 5mm [color="Blue (525nm)" package="5 mm [THT]"]
  LED5_Light_2 = LED - 5mm [color="White (4500K)" package="5 mm [THT]"]

nets:
  N1: Raspberry_Pi_3.GPIO2, R1.Pin_0
  N2: Raspberry_Pi_3.GPIO3, Q1.B
  N3: Raspberry_Pi_3.GIPO4, DS1.DQ
  GND: Raspberry_Pi_3.GND, J1.gnd, VCC1_5v.-, VCC2.-, DS1.GND, Q5.1, Q6.1, LED4_Light_1.C, LED1_heater.cathode, LED2_oxygen_pump.cathode, LED3_second_pump.cathode, LED5_Light_2.cathode
  N4: Raspberry_Pi_3.GIPO17, Q13.B
  N5: Raspberry_Pi_3.GIPO27, R3.Pin_0
  N6: Raspberry_Pi_3.GIPO22, R5.Pin_0
  N7: Raspberry_Pi_3.GIPO10, S2_water_level.leg0
  N8: Raspberry_Pi_3.GIPO9, DHT3.DATA, R8.Pin_1
  N9: Raspberry_Pi_3.GIPO11, DHT2.DATA, R7.Pin_1
  N10: Raspberry_Pi_3.GIPO5, Q3.B
  N11: Raspberry_Pi_3.GIPO6, Q6.0
  N12: Raspberry_Pi_3.GIPO13, Q4.B
  N13: Raspberry_Pi_3.GIPO19, Q5.0
  N14: Raspberry_Pi_3.GIPO26, Q9.B
  N15: Raspberry_Pi_3.GIPO21, Q2.B
  N16: Raspberry_Pi_3.GIPO20, Q8.B
  N17: Raspberry_Pi_3.GIPO16, Q7.B
  N18: Raspberry_Pi_3.GIPO12, Q10.B
  N19: Raspberry_Pi_3.GIPO25, Q11.B
  N20: Raspberry_Pi_3.GIPO24, Q12.B
  N21: Raspberry_Pi_3.GIPO18, J1.pulse
  N22: J1.vcc, Q2.C
  N23: Q2.E, VCC1_5v.+, Q7.C, Q8.C, Q10.C, Q11.C, Q12.C
  VDD: Q1.E, VCC2.+, Q3.E, Q4.E, DHT2.VDD, R7.Pin_0, DHT3.VDD, R8.Pin_0, Q9.C, Q13.E
  N24: Q1.C, R2.pin_1
  N25: R2.pin_0, R1.Pin_1
  N26: DS1.VDD, Q13.C
  N27: Q3.C, R4.pin_1
  N28: R3.Pin_1, R4.pin_0
  N29: Q4.C, R6.pin_1
  N30: R5.Pin_1, R6.pin_0
  N31: Q5.2, DHT2.GND
  N32: Q6.2, DHT3.GND
  N33: Q7.E, LED5_Light_2.anode
  N34: LED4_Light_1.A, Q8.E
  N35: S2_water_level.leg1, Q9.E
  N36: Q10.E, LED1_heater.anode
  N37: Q11.E, LED3_second_pump.anode
  N38: Q12.E, LED2_oxygen_pump.anode

notes:
  Plant light 1
  Pump
  Heater
  Oxygen pump
  Luminosity sensor
  Plant light 2
  Water level sensor
  temperature/himidity sensor
  Water temperature sensor
  5V power source
  3.3V power source
