# Fritzing sketch servomotor (saved by Fritzing 0.9.3b)
breadboards: 1

parts:
  Raspberry_Pi_3 = Raspberry Pi 3 [part_number=RPI-3-V1.2]
  J1 = Basic Servo
  Q2 = NPN-Transistor [package="TO92 [THT]"]

nets:
  N1: Raspberry_Pi_3.3v3, Q2.E
  N2: Raspberry_Pi_3.GIPO22, Q2.B
  GND: Raspberry_Pi_3.GND, J1.gnd
  N3: Raspberry_Pi_3.GIPO18, J1.pulse
  N4: J1.vcc, Q2.C
